# Fritzing sketch WaterMonitoringWiring (saved by Fritzing 0.9.9b)
breadboards: 1

parts:
  U1 = NodeMCU V1.0
  OLED_I2C1 = OLED 128x64 I2C Monochrome Display
  Water_Level_Sensor1 = Water Level Sensor
  WATER_PUMP1 = water pump/motor
  KY-1 = Keyes Relay [package=THT]

nets:
  N1: U1.D1, OLED_I2C1.SCK
  N2: U1.D2, OLED_I2C1.SDA
  3V3: U1.3V3, OLED_I2C1.VDD, Water_Level_Sensor1.VCC, WATER_PUMP1.pin_2, KY-1.signal
  GND: U1.GND, OLED_I2C1.GND, Water_Level_Sensor1.GND, KY-1.power, KY-1.NO
  N3: U1.A0, Water_Level_Sensor1.SIG
  N4: WATER_PUMP1.pin_1, KY-1.C

custom parts:
  NodeMCU V1.0: ESP8266 based NodeMCU
  Water Level Sensor: A water level sensor. This sensor operates at 3V to 5V. The Sig (signal) pin outputs an analogue signal that is in proportion to the amount of water in contact with the sensor.
  water pump/motor: WATER PUMP BY ARDUBLOCKTR
  Keyes Relay: The Keyes 5V relay module is suitable for SCM development, home appliance control. It uses a 5V~12V TIL control signal which can control DC / AC signal.
