# Fritzing sketch WaterPumpWiring (saved by Fritzing 0.9.9b)
breadboards: 1

parts:
  U1 = NodeMCU V1.0
  Capacitive_Soil_Moisture_Sensor1 = DFRobot Capacitive Soil Moisture Sensor V1.0 [part_number=SEN0193]
  KY-1 = Keyes Relay [package=THT]
  WATER_PUMP1 = water pump/motor
  OLED_I2C1 = OLED 128x64 I2C Monochrome Display

nets:
  N1: U1.D1, OLED_I2C1.SCK
  N2: U1.D2, OLED_I2C1.SDA
  N3: U1.D4, KY-1.ground
  3V3: U1.3V3, Capacitive_Soil_Moisture_Sensor1.VCC, KY-1.signal, WATER_PUMP1.pin_2, OLED_I2C1.VDD
  GND: U1.GND, Capacitive_Soil_Moisture_Sensor1.GND, KY-1.power, KY-1.NO, OLED_I2C1.GND
  N4: U1.A0, Capacitive_Soil_Moisture_Sensor1.A
  N5: KY-1.C, WATER_PUMP1.pin_1

custom parts:
  NodeMCU V1.0: ESP8266 based NodeMCU
  DFRobot Capacitive Soil Moisture Sensor V1.0: DFRobot Capacitive Soil Moisture Sensor V1.0 This product measures soil moisture levels by capacitive sensing, rather than resistive sensing like other types of moisture sensor. It is made of a corrosion resistant material giving it a long service life. Insert it into soil and impress your friends with the real-time soil moisture data! The product includes an on-board voltage regulator which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
  Keyes Relay: The Keyes 5V relay module is suitable for SCM development, home appliance control. It uses a 5V~12V TIL control signal which can control DC / AC signal.
  water pump/motor: WATER PUMP BY ARDUBLOCKTR
