# Fritzing sketch WetherStationWireing (saved by Fritzing 0.9.9b)
breadboards: 1

parts:
  OLED_I2C1 = OLED 128x64 I2C Monochrome Display
  Mod2 = KY-018 Photoresistor Module [package="Breakout board"]
  U1 = NodeMCU V1.0
  Part1 = BME280 Breakout

nets:
  N1: OLED_I2C1.SDA, U1.D6, Part1.SDI/SDA
  N2: OLED_I2C1.SCK, U1.D5
  VDD: OLED_I2C1.VDD, Mod2.-, U1.3V3, Part1.3.3V
  GND: OLED_I2C1.GND, Mod2.Vin, U1.GND, Part1.GND
  N3: Mod2.S, U1.A0

custom parts:
  KY-018 Photoresistor Module: KY-018 Photoresistor module, used to measure light intensity. It can determine the presence or absence of light.
  NodeMCU V1.0: ESP8266 based NodeMCU
